# Fritzing sketch Circuit_diagram (saved by Fritzing 0.9.3b)
breadboards: 2

parts:
  Disp1 = LBT2088AH [part_number=LBT2088AH]
  부품1 = Arduino Uno (Rev3) - ICSP
  R1 = Resistor [tolerance=±5% resistance=330 package=THT]
  R2 = Resistor [tolerance=±5% resistance=330 package=THT]
  R3 = Resistor [tolerance=±5% resistance=330 package=THT]
  R4 = Resistor [tolerance=±5% resistance=330 package=THT]
  R5 = Resistor [tolerance=±5% resistance=330 package=THT]
  R6 = Resistor [tolerance=±5% resistance=330 package=THT]
  R8 = Resistor [tolerance=±5% resistance=330 package=THT]
  R9 = Resistor [tolerance=±5% resistance=330 package=THT]
  Part1 = KY-023 Dual Axis Joystick Module [package="Breakout board"]

nets:
  N1: Disp1.pin1, 부품1.A0
  N2: Disp1.pin2, 부품1.A2
  N3: Disp1.pin_3, R2.Pin_1
  N4: Disp1.pin_4, R3.Pin_1
  N5: Disp1.pin_5, 부품1.A3
  N6: Disp1.pin_6, R4.Pin_1
  N7: Disp1.pin_7, 부품1.A1
  N8: Disp1.pin_8, 부품1.D12/MISO
  N9: Disp1.pin_9, 부품1.D10_PWM/SS
  N10: Disp1.pin_10, R5.Pin_1
  N11: Disp1.pin_11, R6.Pin_1
  N12: Disp1.pin_12, 부품1.D13/SCK
  N13: Disp1.pin_13, R1.Pin_1
  N14: Disp1.pin_14, 부품1.D11_PWM/MOSI
  N15: Disp1.pin_15, R9.Pin_1
  N16: Disp1.pin_16, R8.Pin_1
  N17: 부품1.A4/SDA, Part1.VRx
  N18: 부품1.A5/SCL, Part1.VRy
  N19: 부품1.D8, R9.Pin_0
  N20: 부품1.D9_PWM, R8.Pin_0
  N21: 부품1.D2, R1.Pin_0
  N22: 부품1.D3_PWM, R2.Pin_0
  N23: 부품1.D4, R3.Pin_0
  N24: 부품1.D5_PWM, R5.Pin_0
  N25: 부품1.D6_PWM, R4.Pin_0
  N26: 부품1.D7, R6.Pin_0
